# Fritzing sketch Esquema (saved by Fritzing 0.9.1b)
circuit board: 9.28127cm x 5.71989cm

parts:
  L293D = L293D [package=THT]
  Arduino_Uno = Arduino Uno (Rev3)
  Motor_2 = Screw terminal - 2 pins [package=THT]
  Vin_Motores = Screw terminal - 2 pins [package=THT]
  Vin_Arduino = Screw terminal - 2 pins [package=THT]
  Motor_1 = screw terminal, 2 pins [part_number="Motor 1"]
  Jumper = Solder Jumper [package=sj_2w]  # not connected

nets:
  N1: L293D.Enable_1, Arduino_Uno.D11_PWM/MOSI
  N2: L293D.In_1, Arduino_Uno.D12/MISO
  N3: L293D.Out_1_(_Controlled_by_Enable_1_), Motor_2.pin2
  N4: L293D.0V, Arduino_Uno.GND, Vin_Motores.pin2, Vin_Arduino.pin1
  N5: L293D.Out_2_(_Controlled_by_Enable_1_), Motor_2.pin1
  N6: L293D.In_2, Arduino_Uno.D13/SCK
  N7: L293D.Enable_2, Arduino_Uno.D5_PWM
  N8: L293D.In_3, Arduino_Uno.D6_PWM
  N9: L293D.Out_3_(_Controlled_by_Enable_2_), Motor_1.pin2
  N10: L293D.Out_4_(_Controlled_by_Enable_2_), Motor_1.pin1
  N11: L293D.In_4, Arduino_Uno.D7
  N12: L293D.+V, Arduino_Uno.5V
  N13: Arduino_Uno.VIN, Vin_Arduino.pin2
